# Fritzing sketch Wiring Diagram (saved by Fritzing 1.0.6)
circuit board: 8.46667cm x 5.64444cm

parts:
  M1 = ESP32-S3-DevKitC-1-N8R8-v1 [part_number=ESP32-S3-DevKitC-1-N8R8-v1]
  F_Sharp = Header 3 [package=screwterminal-3.5mm-3_lock.007s]
  R_Encoder = Header 4 [package=screwterminal-3.5mm-4_lock]
  R_Sharp = Header 3 [package=screwterminal-3.5mm-3_lock.007s]
  L_Sharp = Header 3 [package=screwterminal-3.5mm-3_lock.007s]
  L_Motor = Header 3 [package=screwterminal-3.5mm-3_lock.007s]
  R_Motor = Header 3 [package=screwterminal-3.5mm-3_lock.007s]
  IMU = Header 4 [package=screwterminal-3.5mm-4_lock]
  L_Encoder = Header 4 [package=screwterminal-3.5mm-4_lock]

nets:
  N1: M1.pin_1, M1.pin_2, IMU.2
  N2: M1.pin_4, R_Motor.3
  N3: M1.pin_5, R_Motor.2
  N4: M1.pin_6, R_Motor.1
  N5: M1.pin_7, L_Motor.3
  N6: M1.pin_8, L_Motor.2
  N7: M1.pin_9, L_Motor.1
  N8: M1.pin_10, L_Encoder.1
  N9: M1.pin_11, L_Encoder.3
  N10: M1.pin_12, IMU.3
  N11: M1.pin_15, IMU.4
  N12: M1.pin_16, R_Encoder.3
  N13: M1.pin_17, R_Encoder.1
  N14: M1.pin_18, R_Sharp.1
  N15: M1.pin_19, L_Sharp.1
  N16: M1.pin_20, F_Sharp.1
  N17: M1.pin_21, F_Sharp.3, R_Encoder.4, R_Sharp.3, L_Sharp.3, L_Encoder.4
  N18: M1.pin_22, F_Sharp.2, R_Encoder.2, R_Sharp.2, L_Sharp.2, IMU.1, L_Encoder.2

notes:
  UA
  I1
  UB
  I2
  I3
  I4
  5V
  L Motor
  R Motor
  GND
  B
  A
  L Encoder
  R Encoder
  F Sharp
  L Sharp
  R Sharp
  S
  PINOUTS: (GPIO -> OUTPUT)
  F Sharp (14 -> S) ANALOG 0-3.3V
  L Sharp (13 -> S) ANALOG 0-3.3V
  R Sharp (12 -> S) ANALOG 0-3.3V
  L Encoder (10 -> A, 11 -> B) INTERUPT
  R Encoder (18 -> A, 17 -> B) INTERUPT
  L Motor (16 -> UA, 15 -> I1, 7 -> I2) PWM H-L H-L
  R Motor (9 -> UB, 5 -> I3, 4 -> I4) PWM H-L H-L
  IMU (SDA -> 8, SCL ->9) I2C
  IMU
  SDA
  3.3V
  SCL

custom parts:
  ESP32-S3-DevKitC-1-N8R8-v1: ESP32-S3-DevKitC-1-N8R8-v1 This module is 44pins long (2x22) and 11 pins width.
